# Fritzing sketch hshb_hardware (saved by Fritzing 0.8.7b)
stripboards: 2

parts:
  Bauteil1 = Arduino Due (Rev2b)
  Bauteil2 = Arduino Due (Rev2b)
  NEOPIXEL1 = Neopixel Strip -- White (60/m)
  NEOPIXEL2 = Neopixel Strip -- White (60/m)
  NEOPIXEL3 = Neopixel Strip -- White (60/m)
  R1 = Resistor [tolerance=±5% resistance=10k package=THT]
  R2 = Resistor [tolerance=±5% resistance=10k package=THT]
  R3 = Resistor [tolerance=±5% resistance=10k package=THT]
  R4 = Resistor [tolerance=±5% resistance=10k package=THT]
  R5 = Resistor [tolerance=±5% resistance=10k package=THT]
  R6 = Resistor [tolerance=±5% resistance=10k package=THT]
  R7 = Resistor [tolerance=±5% resistance=10k package=THT]
  R8 = Resistor [tolerance=±5% resistance=10k package=THT]
  R9 = Resistor [tolerance=±5% resistance=10k package=THT]
  R10 = Resistor [tolerance=±5% resistance=10k package=THT]
  R11 = Resistor [tolerance=±5% resistance=10k package=THT]
  R12 = Resistor [tolerance=±5% resistance=10k package=THT]
  R13 = Resistor [tolerance=±5% resistance=10k package=THT]
  R14 = Resistor [tolerance=±5% resistance=10k package=THT]

nets:
  N1: Bauteil1.D14/TX3, Bauteil2.D15/RX3
  N2: Bauteil1.D15/RX3, Bauteil2.D14/TX3
  N3: Bauteil1.D22, R7.Pin_0
  N4: Bauteil1.D24, R6.Pin_0
  N5: Bauteil1.D26, R5.Pin_0
  N6: Bauteil1.D28, R4.Pin_0
  N7: Bauteil1.D30, R3.Pin_0
  N8: Bauteil1.D32, R2.Pin_0
  N9: Bauteil1.D34, R1.Pin_0
  N10: Bauteil1.D36, R9.Pin_0
  N11: Bauteil1.D38, R12.Pin_0
  N12: Bauteil1.D40, R11.Pin_0
  N13: Bauteil1.D42, R8.Pin_0
  N14: Bauteil1.D44, R13.Pin_0
  N15: Bauteil1.D46, R14.Pin_0
  N16: Bauteil1.D48, R10.Pin_0
  N17: Bauteil2.D2_PWM, NEOPIXEL1.+5V#1
  N18: NEOPIXEL1.+5V#6, NEOPIXEL2.+5V#1
  N19: NEOPIXEL2.+5V#6, NEOPIXEL3.+5V#1
  N20: R1.Pin_1, R2.Pin_1, R3.Pin_1, R4.Pin_1, R5.Pin_1, R6.Pin_1, R7.Pin_1
  N21: R8.Pin_1, R9.Pin_1, R10.Pin_1, R11.Pin_1, R12.Pin_1, R13.Pin_1, R14.Pin_1

notes:
  Input / Music
  Game / Display
  ...
  WS2812 LED strips
  90x16 zigzag matrix
  BLUE
  RED
  YELLOW
  JS UP
  JS LEFT
  JS DOWN
  JS RIGHT
  P1 controls
  P2 controls
  +5V

custom parts:
  Neopixel Strip -- White (60/m): Neopixel Strip, White, 60 pixels per meter.
